# Fritzing sketch ktinga (saved by Fritzing 0.9.4)
breadboards: 1

parts:
  U1 = attiny85 [package=dip]
  LED1 = smd LED [color="Red (633nm)" package="0805 [SMD]"]
  R2 = Resistor [tolerance=±5% resistance=100 package="0402 [SMD]"]
  R3 = Resistor [tolerance=±5% resistance=100 package="0402 [SMD]"]
  LED2 = smd LED [color="Red (633nm)" package="0805 [SMD]"]
  LED3 = smd LED [color="White (8000K)" package="0805 [SMD]"]
  R4 = Resistor [tolerance=±5% resistance=100 package="0402 [SMD]"]
  U2 = attiny85 [package=dip]
  S1 = Pushbutton [package="[SMD]"]
  R5 = Resistor [tolerance=±0.05% resistance=10k package="0805 [SMD]"]

nets:
  N1: U1.Pin_5, R3.Pin_0
  N2: U1.Pin_6, R2.Pin_0
  N3: U1.Pin_8, U2.Pin_8, R5.Pin_0
  N4: LED1.cathode, R2.Pin_1
  N5: R3.Pin_1, LED2.cathode
  N6: LED2.anode, LED3.anode, S1.Pin_3, S1.Pin_4
  N7: LED3.cathode, R4.Pin_1
  N8: R4.Pin_0, U2.Pin_5
  N9: U2.Pin_7, S1.Pin_1, S1.Pin_2, R5.Pin_1
